# Fritzing sketch rpi_controller_v2 (saved by Fritzing 0.9.3b)
circuit board: 9.6cm x 7.2cm
breadboards: 1

parts:
  Raspberry_Pi = Raspberry Pi 3 [part_number=RPI-3-V1.2]
  R1 = Resistor [tolerance=±5% resistance=220 package=THT]
  LED1 = LED - 5mm [color="Red (633nm)" package="5 mm [THT]"]
  R2 = Resistor [tolerance=±5% resistance=220 package=THT]
  LED2 = LED - 5mm [color="Red (633nm)" package="5 mm [THT]"]
  LED3 = LED - 5mm [color="Red (633nm)" package="5 mm [THT]"]
  R3 = Resistor [tolerance=±5% resistance=220 package=THT]
  LED4 = LED - 5mm [color="Red (633nm)" package="5 mm [THT]"]
  R4 = Resistor [tolerance=±5% resistance=220 package=THT]
  LED5 = LED - 5mm [color="Red (633nm)" package="5 mm [THT]"]
  R5 = Resistor [tolerance=±5% resistance=220 package=THT]
  LED6 = LED - 5mm [color="Red (633nm)" package="5 mm [THT]"]
  R6 = Resistor [tolerance=±5% resistance=220 package=THT]
  RGB_LED = RGB LED - (4 legs) [package="5 mm [THT]"]
  R7 = Resistor [tolerance=±5% resistance=220 package=THT]
  S6 = Pushbutton [package="[THT]"]
  S5 = Pushbutton [package="[THT]"]
  S2 = Pushbutton [package="[THT]"]
  S4 = Pushbutton [package="[THT]"]
  S1 = Pushbutton [package="[THT]"]
  S3 = Pushbutton [package="[THT]"]
  J1 = Piezo Speaker
  Q1 = NPN-Transistor [package="TO92 [THT]"]

nets:
  3V3: Raspberry_Pi.3v3, Raspberry_Pi.3V3, R1.Pin_1, R2.Pin_1, R3.Pin_1, R4.Pin_1, R5.Pin_1, R6.Pin_1, R7.Pin_1, S6.Pin_3, S6.Pin_4, S5.Pin_3, S5.Pin_4, S2.Pin_3, S2.Pin_4, S4.Pin_3, S4.Pin_4, S1.Pin_3, S1.Pin_4, S3.Pin_3, S3.Pin_4
  N1: Raspberry_Pi.GIPO4, S5.Pin_1
  N2: Raspberry_Pi.GIPO17, S6.Pin_1
  N3: Raspberry_Pi.GIPO27, Q1.B
  N4: Raspberry_Pi.GND, J1.pin2
  N5: Raspberry_Pi.GIPO5, S1.Pin_1, S1.Pin_2
  N6: Raspberry_Pi.GIPO6, S2.Pin_1, S2.Pin_2
  N7: Raspberry_Pi.GIPO13, S4.Pin_1, S4.Pin_2
  N8: Raspberry_Pi.GIPO19, S3.Pin_1, S3.Pin_2
  N9: Raspberry_Pi.GIPO21, LED1.cathode
  N10: Raspberry_Pi.GIPO20, LED2.cathode
  N11: Raspberry_Pi.GIPO16, LED3.cathode
  N12: Raspberry_Pi.GIPO12, LED4.cathode
  N13: Raspberry_Pi.GIPO7, LED5.cathode
  N14: Raspberry_Pi.GIPO8, LED6.cathode
  N15: Raspberry_Pi.GIPO18, RGB_LED.blue_cathode
  N16: Raspberry_Pi.GIPO15, RGB_LED.green_cathode
  N17: Raspberry_Pi.GIPO14, RGB_LED.red_cathode
  N18: Raspberry_Pi.5V, Q1.C
  N19: R1.Pin_0, LED1.anode
  N20: R2.Pin_0, LED2.anode
  N21: LED3.anode, R3.Pin_0
  N22: LED4.anode, R4.Pin_0
  N23: LED5.anode, R5.Pin_0
  N24: LED6.anode, R6.Pin_0
  N25: RGB_LED.common_anode, R7.Pin_0
  N26: J1.pin1, Q1.E

notes:
  Raspberry PI controller v2
  Dr. Ir. W.A.P. van Kleunen
